# Fritzing sketch l298n_schematics (saved by Fritzing 0.9.4)
breadboards: 1

parts:
  Raspberry_Pi_1 = Raspberry Pi 3 [part_number=RPI-3-V1.2]
  S1 = H-Bridge with L298N
  M1 = DC Motor
  VCC1 = Battery block 9V

nets:
  GND: Raspberry_Pi_1.GPIO4, Raspberry_Pi_1.GND, Raspberry_Pi_1.GPIO15, S1.GND, VCC1.-
  N1: Raspberry_Pi_1.GPIO25, S1.IN2
  N2: Raspberry_Pi_1.GPIO24, S1.IN1
  N3: Raspberry_Pi_1.GPIO23, S1.ENA
  N4: S1.12V, VCC1.+
  N5: S1.M1-01, M1.pin_1
  N6: S1.M1-02, M1.pin_2

custom parts:
  H-Bridge with L298N: h-bridge
